// Logisim project ALU.circ as structural Verilog: 1 circuit, main circuit ALU
module ALU (
  input  [31:0] A,
  input  [31:0] B,
  input  [4:0] Shift,
  input  [3:0] Codop,
  input  CarryIn,
  output [31:0] S,
  output [3:0] Flags
);

  wire ADC_C, and_4_out, bitselector_1_out, bitselector_2_out, CMN_C, CMP_C, not_1_out, not_4_out, not_5_out,
       or_2_out, RSB_C, SBC_C;
  wire [4:0] subtractor_4_out, subtractor_5_out;
  wire [31:0] adder_1_out, adder_2_out, and_1_out, and_2_out, and_3_out, multiplexer_1_out, multiplier_1_out,
       not_2_out, not_3_out, or_1_out, shifter_1_out, shifter_2_out, shifter_3_out, shifter_4_out,
       subtractor_1_out, subtractor_2_out, subtractor_3_out, xor_1_out;

  assign and_1_out = A & B;  // AND_Gate and_1, 32 bits wide
  assign xor_1_out = B ^ A;  // XOR_Gate xor_1, 32 bits wide
  Shifter #(.width(32)) shifter_1 (.in(B), .\dist (Shift), .out(shifter_1_out));
  Shifter #(.shift("lr"), .width(32)) shifter_2 (.in(B), .\dist (Shift), .out(shifter_2_out));
  Shifter #(.shift("ar"), .width(32)) shifter_3 (.in(B), .\dist (Shift), .out(shifter_3_out));
  Adder #(.width(32)) adder_1 (.a(A), .b(B), .out(adder_1_out), .cin(CarryIn), .cout(ADC_C));
  not not_1 (not_1_out, CarryIn);
  Subtractor #(.width(32)) subtractor_1 (.a(B), .b(A), .out(subtractor_1_out), .bin(not_1_out), .bout(SBC_C));
  Shifter #(.shift("rr"), .width(32)) shifter_4 (.in(B), .\dist (Shift), .out(shifter_4_out));
  Subtractor #(.width(32)) subtractor_2 (.a({32{1'b0}}), .b(A), .out(subtractor_2_out), .bout(RSB_C));  // open: bin
  Subtractor #(.width(32)) subtractor_3 (.a(B), .b(A), .out(subtractor_3_out), .bout(CMP_C));  // open: bin
  Adder #(.width(32)) adder_2 (.a(B), .b(A), .out(adder_2_out), .cout(CMN_C));  // open: cin
  assign or_1_out = B | A;  // OR_Gate or_1, 32 bits wide
  Multiplier #(.width(32)) multiplier_1 (.a(B), .b(A), .out(multiplier_1_out));  // open: cin, cout
  assign not_2_out = ~A;  // NOT_Gate not_2, 32 bits wide
  assign not_3_out = ~A;  // NOT_Gate not_3, 32 bits wide
  assign and_2_out = A & B;  // AND_Gate and_2, 32 bits wide
  assign and_3_out = B & not_2_out;  // AND_Gate and_3, 32 bits wide
  Multiplexer #(.select(4), .width(32)) multiplexer_1 (
    .in0(and_1_out), .in1(xor_1_out), .in2(shifter_1_out), .in3(shifter_2_out), .in4(shifter_3_out),
    .in5(adder_1_out), .in6(subtractor_1_out), .in7(shifter_4_out), .in8(and_2_out), .in9(subtractor_2_out),
    .in10(subtractor_3_out), .in11(adder_2_out), .in12(or_1_out), .in13(multiplier_1_out), .in14(and_3_out),
    .in15(not_3_out), .out(multiplexer_1_out), .sel(Codop));
  not not_4 (not_4_out, Codop[0]);
  not not_5 (not_5_out, Codop[2]);
  or or_2 (or_2_out, not_4_out, Codop[1]);
  BitSelector #(.width(32)) bitselector_1 (.in(B), .out(bitselector_1_out), .sel(subtractor_4_out));
  Subtractor #(.width(5)) subtractor_4 (.a({5{1'b0}}), .b(Shift), .out(subtractor_4_out));  // open: bin, bout
  BitSelector #(.width(32)) bitselector_2 (.in(B), .out(bitselector_2_out), .sel(subtractor_5_out));
  Subtractor #(.width(5)) subtractor_5 (.a(Shift), .b({5{1'b1}}), .out(subtractor_5_out));  // open: bin, bout
  and and_4 (and_4_out, or_2_out, not_5_out, Codop[3]);
  Multiplexer #(.width(32)) multiplexer_2 (.in0(multiplexer_1_out), .in1(B), .out(S), .sel(and_4_out));
  Comparator #(.width(32)) comparator_1 (
    .a(multiplexer_1_out), .b({32{1'b0}}), .eq(Flags[2]), .lt(Flags[3]));  // open: gt
  Multiplexer #(.select(4)) multiplexer_3 (
    .in0(1'b0), .in1(1'b0), .in2(bitselector_1_out), .in3(bitselector_2_out), .in4(bitselector_2_out),
    .in5(ADC_C), .in6(SBC_C), .in7(B[31]), .in8(1'b0), .in9(RSB_C), .in10(CMP_C), .in11(CMN_C), .in12(1'b0),
    .in14(1'b0), .in15(1'b0), .out(Flags[1]), .sel(Codop));  // open: in13

  // Notes on the sheet:
  //   Note: for ROR, C = N
  //   Note 2: assume that shift > 0 for LSL and LSR
endmodule
